# Fritzing sketch schema (saved by Fritzing 0.9.3b)

parts:
  L298N2 = L298N DC motor driver
  M2 = DC Motor  # not connected
  S1 = SPST Switch [package=switch-spdt_kit]
  VCC1 = Battery
  D1 = Schottky Diode [part_number=1N5817 package="300 mil [THT]"]
  Part1 = Solar Panel [package="Renogy 50 Watts 12 Volt Monocrystalline Bendable Solar Panel"]
  S2 = SPST Switch [package=switch-spdt]
  Part2 = Soil Moisture Sensor
  U1 = ESP32-38PinWide [part_number=ESP32-38PinWide]
  Part3 = Humidity Sensor - HIH-4030 Breakout

nets:
  N1: L298N2.12V, S1.O, S1.P
  GND: L298N2.GND, VCC1.-, Part1.Connector_2, Part2.GND, U1.GPIO11, Part3.GND
  N2: L298N2.ENA, U1.GPIO14
  N3: L298N2.IN1, U1.GPIO27
  N4: L298N2.IN2, U1.GPIO26
  N5: S1.S, VCC1.+, S2.O
  N6: D1.cathode, Part1.Connector_1
  N7: D1.anode, S2.S
  VCC: Part2.VCC, U1.VIN, Part3.VCC
  N8: Part2.SIG, U1.GPIO39
  N9: U1.GPIO34, Part3.OUT

custom parts:
  L298N DC motor driver: 2x DC motor driver with 78M05 positive voltage regulator (7..35 V) L298N: max 46 V, 2 A Set 5 V Enable jumper to enable 5 V regultor (needed for the L298N) and +5 V output at screw terminal or supply external +5 V at screw terminal Set ENA and/or ENB to +5 V to enable motor permanently or supply ENA and/or ENB with PWM signal IN1 and IN2 set rotation directory for motor A (OUT1/OUT2) IN2 and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
  Battery: Your standard 2x 18650 battery pack (7,4 Volts)
  Solar Panel: Renogy 50 Watts 12 Volt Solar Panel
  ESP32-38PinWide: Generic 38-Pin ESP32 with wide format (only access to one side of pins on a breadboard) based on Stephen Lilley's HiLetgo ESP-WROOM-32 ESP32 ESP-32S Development Board.
